// Digital circuit ALU.dig as structural Verilog
module ALU (
  input  [31:0] A,
  input  [31:0] B,
  input  Clock,
  input  AWe,
  input  BWe,
  input  Oe,
  input  [2:0] OPSELECT,
  output [31:0] O
);

  wire Adder_c_o, and_1_out, and_2_out, decoder_1_out_1, decoder_1_out_5, decoder_1_out_6, or_1_out, or_2_out;
  wire [0:0] not_2_out, xor_1_out;
  wire [31:0] A_q, Adder_s, and_3_out, B_q, multiplexer_1_out, multiplexer_2_out, not_1_out, or_3_out,
       xor_2_out;

  Decoder #(.Selector_Bits(3)) decoder_1 (
    .sel(OPSELECT), .out_1(decoder_1_out_1), .out_5(decoder_1_out_5), .out_6(decoder_1_out_6));  // open: out_0, out_2, out_3, out_4, out_7
  Register #(.Bits(32)) u_A (.D(A), .C(Clock), .en(AWe), .Q(A_q));
  Register #(.Bits(32)) u_B (.D(B), .C(Clock), .en(BWe), .Q(B_q));
  assign not_1_out = ~B_q;  // Not not_1, 32 bits wide
  or or_1 (or_1_out, decoder_1_out_1, decoder_1_out_5, decoder_1_out_6);
  and and_1 (and_1_out, ~A_q[31], B_q[31], Adder_s[31]);  // And
  Multiplexer #(.Bits(32)) multiplexer_1 (.sel(or_1_out), .in_0(B_q), .in_1(not_1_out), .out(multiplexer_1_out));
  or or_2 (or_2_out, and_1_out, and_2_out);
  and and_2 (and_2_out, A_q[31], ~B_q[31], ~Adder_s[31]);  // And
  xor xor_1 (xor_1_out[0], or_2_out, Adder_s[31]);
  Add #(.Bits(32)) Adder (.a(A_q), .b(multiplexer_1_out), .c_i(or_1_out), .s(Adder_s), .c_o(Adder_c_o));
  assign and_3_out = A_q & multiplexer_1_out;  // And and_3, 32 bits wide
  assign or_3_out = A_q | multiplexer_1_out;  // Or or_3, 32 bits wide
  assign xor_2_out = A_q ^ multiplexer_1_out;  // XOr xor_2, 32 bits wide
  not not_2 (not_2_out[0], Adder_c_o);
  Multiplexer #(.Bits(32), .Selector_Bits(3)) multiplexer_2 (
    .sel(OPSELECT), .in_0(Adder_s), .in_1(Adder_s), .in_2(and_3_out), .in_3(or_3_out), .in_4(xor_2_out),
    .in_5({{31{1'b0}}, not_2_out[0]}), .in_6({{31{1'b0}}, xor_1_out[0]}), .in_7({32{1'b0}}),
    .out(multiplexer_2_out));
  assign O = Oe ? multiplexer_2_out : 32'bz;  // Driver driver_1

  // Notes on the sheet:
  //   OPSELECT: 000:add
  //   001:sub
  //   010:and
  //   011:or
  //   100:xor
  //   101:comUnsigned
  //   110:comSigned
  //   000:add
  //   001:sub
  //   010:and
  //   011:or
  //   100:xor
  //   101:comUnsigned
  //   110:comSigned
endmodule
